# Fritzing sketch ESP8266 D1 mini Pro Schaltplan (saved by Fritzing 0.9.4)
breadboards: 1

parts:
  WeMos_D1_Mini1 = WeMos D1 Mini
  LED1 = LED - 3mm [color="Blue (430nm)" package="3 mm [THT]"]
  LEDs = LED - 3mm [color="Blue (430nm)" package="3 mm [THT]"]
  R1 = Resistor [tolerance=±5% resistance=220 package=THT]
  R2 = Resistor [tolerance=±5% resistance=220 package=THT]
  Widerstände = Resistor [tolerance=±5% resistance=220 package=THT]
  S0_Schnittstelle_1 = Screw terminal - 2 pins [package=THT]
  S0_Schnittstelle_3 = Screw terminal - 2 pins [package=THT]
  S0_Schnittstelle_2 = Screw terminal - 2 pins [package=THT]
  OLED_Display_128x96_I2C = Module display OLED I2C 128x64 SSD1306 [package=THT]
  part = LED - 3mm [color="Blue (430nm)" package="3 mm [THT]"]

nets:
  N1: WeMos_D1_Mini1.3V3, R1.Pin_0, R2.Pin_0, Widerstände.Pin_0
  5V: WeMos_D1_Mini1.5V, OLED_Display_128x96_I2C.VCC
  N2: WeMos_D1_Mini1.D1, OLED_Display_128x96_I2C.SCL
  N3: WeMos_D1_Mini1.D2, OLED_Display_128x96_I2C.SDA
  N4: WeMos_D1_Mini1.D5, LEDs.cathode, S0_Schnittstelle_3.pin1
  N5: WeMos_D1_Mini1.D6, LED1.cathode, S0_Schnittstelle_2.pin1
  N6: WeMos_D1_Mini1.D7, S0_Schnittstelle_1.pin1, part.cathode
  GND: WeMos_D1_Mini1.G, S0_Schnittstelle_1.pin2, S0_Schnittstelle_3.pin2, S0_Schnittstelle_2.pin2, OLED_Display_128x96_I2C.GND
  N7: LED1.anode, R1.Pin_1
  N8: LEDs.anode, Widerstände.Pin_1
  N9: R2.Pin_1, part.anode

custom parts:
  Module display OLED I2C 128x64 SSD1306: Ecran OLED I2C SSD163 de 128x64 avec connexion I2C
